# Fritzing sketch Smart Room Controller (saved by Fritzing 0.9.9b)
breadboards: 3

parts:
  Breadboard4 = Breadboard Split Power
  Breadboard5 = Breadboard Split Power
  Teensy_3_1 = Teensy 3.1
  RG_encoder1 = SprkFn RG Encoder [package="DIP (Dual Inline) [THT]"]
  C1 = Capacitor [package=cap-pth-small2]
  C2 = Capacitor [package=cap-pth-small2]
  WIZ820io1 = WIZ820io [part_number=WIZ820io]
  OLED_I2C1 = OLED 128x64 I2C Monochrome Display
  S1 = Pushbutton [package="[THT]"]
  S2 = Pushbutton [package="[THT]"]
  R1 = Resistor [tolerance=±5% power=0.25 resistance=10k package=THT]
  R2 = Resistor [tolerance=±5% power=0.25 resistance=10k package=THT]
  R3 = Photocell (LDR) [package=THT]  # not connected

nets:
  GND: Breadboard4.pin3Z, Breadboard4.pin13Z, Breadboard4.pin20Z, Breadboard4.pin29Z, Breadboard5.pin3Z, Breadboard5.pin11Z, Breadboard5.pin28Z, Teensy_3_1.GND, RG_encoder1.GND, RG_encoder1.B, C1.2, C2.1, WIZ820io1.GND, OLED_I2C1.GND, R1.Pin_1, R2.Pin_1
  3V3: Breadboard4.pin4Y, Breadboard4.pin15Y, Breadboard4.pin17Y, Breadboard4.pin21Y, Breadboard4.pin29Y, Breadboard5.pin3Y, Breadboard5.pin15Y, Breadboard5.pin17Y, Breadboard5.pin29Y, Teensy_3_1.3V3, WIZ820io1.VIN, OLED_I2C1.VDD, S1.Pin_1, S1.Pin_2, S2.Pin_1, S2.Pin_2
  N1: Teensy_3_1.D9, WIZ820io1.nRESET
  N2: Teensy_3_1.D10, WIZ820io1.nSS
  N3: Teensy_3_1.D11, WIZ820io1.MOSI
  N4: Teensy_3_1.D12, WIZ820io1.MISO
  N5: Teensy_3_1.D13, WIZ820io1.SCLK
  N6: Teensy_3_1.A1/D15, S2.Pin_3, S2.Pin_4, R1.Pin_0
  N7: Teensy_3_1.A2/D16, S1.Pin_3, S1.Pin_4, R2.Pin_0
  N8: Teensy_3_1.A3/D17, RG_encoder1.+G
  N9: Teensy_3_1.A4/D18, OLED_I2C1.SDA
  N10: Teensy_3_1.A5/D19, OLED_I2C1.SCK
  N11: Teensy_3_1.A6/D20, RG_encoder1.+R
  N12: Teensy_3_1.A7/D21, RG_encoder1.A, C1.1
  N13: Teensy_3_1.A8/D22, RG_encoder1.C, C2.2
  N14: Teensy_3_1.A9/D23, RG_encoder1.SW

custom parts:
  Breadboard Split Power: A custom 6 pin per group power supply strip where the top row (ground) is all bussed together and the bottom row (+V) is split in two groups of 12 pins. This version is modified to be a loadable part and was rescaled to be on the standard 1px = 1thou grid with the size set in inches
  SprkFn RG Encoder: SparkFun RG Rotary Encoder
  Pushbutton: A generic pushbutton.
  Pushbutton: A generic pushbutton.
